# Fritzing sketch Relay (saved by Fritzing 0.8.5b)
circuit board: 4.64255cm x 2.63877cm
breadboards: 1

parts:
  Componente1 = Relay T73
  D1 = Rectifier Diode [part_number=1N4001 package="300 mil [THT]"]
  Q1 = NPN-Transistor [package="TO92 [THT]"]
  R1 = Resistor [tolerance=±5% resistance=220 package=THT]
  R2 = Resistor [tolerance=±5% resistance=220 package=THT]
  LED1 = LED - 5mm [color="Red (633nm)" package="5 mm [THT]"]
  J1 = Screw terminal - 2 pins [package=THT]
  J2 = female pin header, 3 pins [form="♀ (female)"]

nets:
  N1: Componente1.C1, D1.anode, Q1.C, LED1.cathode
  N2: Componente1.C2, D1.cathode, R2.Pin_0, J2.pin1
  N3: Componente1.COM, J1.pin1
  N4: Componente1.NO, J1.pin2
  N5: Q1.E, J2.pin3
  N6: Q1.B, R1.Pin_1
  N7: R1.Pin_0, J2.pin2
  N8: R2.Pin_1, LED1.anode

notes:
  J.Victor

custom parts:
  Relay T73: An T73 Mini PCB Relay
