# Fritzing sketch Shield Progra (saved by Fritzing 0.9.0b)
circuit board: 7.44451cm x 5.41859cm
breadboards: 1

parts:
  U1 = atmega328 [package=dip]
  U2 = ATmega644 [package=pdpi]
  Attiny85/45 = attiny85 [package=dip]
  Attiny_2313 = IC, DIP package, 20 pins [chip_label=IC]
  HeartBeat = LED - 5mm [color="Yellow (595nm)" package="5 mm [THT]"]
  Progrsso = LED - 5mm [color="Green (570nm)" package="5 mm [THT]"]
  Error = LED - 5mm [color="Red (633nm)" package="5 mm [THT]"]
  Blink = LED - 5mm [color="Red (633nm)" package="5 mm [THT]"]
  R1 = Resistor [tolerance=±5% resistance=120 package=THT]
  R3 = Resistor [tolerance=±5% resistance=120 package=THT]
  C1 = Electrolytic Capacitor [capacitance=1µF package="100 mil [THT, electrolytic]"]
  XTAL1 = Crystal [frequency="16 Mhz" package=THT]
  C3 = Ceramic Capacitor [capacitance=100nF package="100 mil [THT, multilayer]"]
  C2 = Ceramic Capacitor [capacitance=100nF package="100 mil [THT, multilayer]"]
  Attiny84/44 = IC, DIP package, 14 pins [chip_label=IC]
  Componente1 = Arduino Uno (Rev3)

nets:
  N1: U1.RESET, U2.RESET, Attiny85/45.Pin_1, Attiny_2313.pin1, Attiny84/44.pin4, Componente1.D10_PWM/SS
  5V: U1.VCC, U1.AVCC, U2.VCC, Attiny85/45.Pin_8, Attiny_2313.pin20, Attiny84/44.pin1, Componente1.5V
  GND: U1.GND, U2.GND, Attiny85/45.Pin_4, Attiny_2313.pin10, R1.Pin_0, R3.Pin_0, C1.-, C3.0, C2.0, Attiny84/44.pin14, Componente1.GND
  N2: U1.XLAT1, XTAL1.pin_1, C3.1
  N3: U1.XLAT2, XTAL1.pin_0, C2.1
  N4: U1.D9_(PWM), U2.PD5, Attiny85/45.Pin_3, Attiny_2313.pin16, Blink.anode, Attiny84/44.pin13
  N5: U1.D11_(PWM), U2.PB5, Attiny85/45.Pin_5, Attiny_2313.pin17, Attiny84/44.pin7, Componente1.D11_PWM/MOSI
  N6: U1.D12, U2.PB6, Attiny85/45.Pin_6, Attiny_2313.pin18, Attiny84/44.pin8, Componente1.D12/MISO
  N7: U1.D13, U2.PB7, Attiny85/45.Pin_7, Attiny_2313.pin19, Attiny84/44.pin9, Componente1.D13/SCK
  N8: U2.PA6, U2.PA5
  N9: HeartBeat.cathode, Progrsso.cathode, Error.cathode, R1.Pin_1
  N10: HeartBeat.anode, Componente1.D9_PWM
  N11: Progrsso.anode, Componente1.D7
  N12: Error.anode, Componente1.D8
  N13: Blink.cathode, R3.Pin_1
  N14: C1.+, Componente1.RESET

notes:
  Atmega 328/8/32/16
  j.victoresp@gmail.com
  Atmega8/328
  https://github.com
  /JoaoVictorO/Attiny_Shield
